# Fritzing sketch amplifier_mqtt (saved by Fritzing 0.9.4)

parts:
  WeMos_D1_Mini1 = WeMos D1 Mini
  HLK-PM1 = HLK-PM12 [part_number=HLK-PM12]
  Factory_power_button = Pushbutton [package="[THT]"]
  Factory_AC_power = Power plug
  Relay_module = WeMos D1 Mini Relay Shield
  Factory_USB_port = USB connector [package=THT]

nets:
  5V: WeMos_D1_Mini1.5V, HLK-PM1.+Vo, Relay_module.5V
  N1: WeMos_D1_Mini1.D1, Relay_module.D1
  N2: WeMos_D1_Mini1.D2, Factory_USB_port.5V
  N3: WeMos_D1_Mini1.G, HLK-PM1.-Vo, Relay_module.G, Factory_USB_port.GND, Factory_USB_port.chassis5, Factory_USB_port.chassis6
  N4: HLK-PM1.AC_1, Factory_AC_power.VCC
  N5: HLK-PM1.AC_2, Factory_AC_power.GND
  N6: Factory_power_button.Pin_1, Relay_module.COM
  N7: Factory_power_button.Pin_3, Relay_module.NO

notes:
  10K
