# Fritzing sketch ir_remote_mqtt (saved by Fritzing 0.9.4)

parts:
  WeMos_D1_Mini1 = WeMos D1 Mini  # not connected
  WeMos_IR_Shield = WeMos D1 Mini Protoboard Shield
  HLK-PM1 = HLK-PM01
  AC_TV_Power = Power plug
  TV_IR_Receiver = TSOP312.., 314.. [package=THT]  # not connected

nets:
  N1: WeMos_IR_Shield.5V, HLK-PM1.+Vo
  N2: WeMos_IR_Shield.G, HLK-PM1.-Vo
  N3: HLK-PM1.AC#0, AC_TV_Power.VCC
  N4: HLK-PM1.AC#1, AC_TV_Power.GND
